# Fritzing sketch EFDURCWHAbAU-Fritzing (saved by Fritzing 0.9.3b)
circuit board: 31.1082cm x 18.8786cm

parts:
  DHT1 = DHT22 Humidity and Temperature Sensor
  LCD1 = LCD screen
  R1 = Resistor [tolerance=±5% resistance=10k package=THT]
  LCM1602_IIC1 = LCM1602 IIC [part_number="LCM1602 IIC" chip_label="LCM1602 IIC" package="DIP (Dual Inline) [THT]"]
  Q2 = TRANSISTOR_NPN [package=to-92-ammo]
  F1 = Fan - Ventilador [package=THT]
  VCC1 = Battery block 9V
  KF-1 = KF-301 Relay [package=THT]
  Part3 = Lilypad Battery Connect
  LED2 = LEDs [package=led10mm]
  Part1 = Arduino Uno (Rev3)

nets:
  VDD: DHT1.VDD, R1.Pin_1, LCM1602_IIC1.VCC, KF-1.power, Part1.5V
  N1: DHT1.DATA, R1.Pin_0, Part1.D2
  GND: DHT1.GND, LCM1602_IIC1.GND, KF-1.ground, Part1.GND
  VSS: LCD1.VSS, LCM1602_IIC1.VSS
  VDD_2: LCD1.VDD, LCM1602_IIC1.VDD
  N2: LCD1.V0, LCM1602_IIC1.V0
  N3: LCD1.RS, LCM1602_IIC1.RS
  N4: LCD1.R/W, LCM1602_IIC1.RW
  N5: LCD1.E, LCM1602_IIC1.E
  N6: LCD1.DB0, LCM1602_IIC1.D0
  N7: LCD1.DB1, LCM1602_IIC1.D1
  N8: LCD1.DB2, LCM1602_IIC1.D2
  N9: LCD1.DB3, LCM1602_IIC1.D3
  N10: LCD1.DB4, LCM1602_IIC1.D4
  N11: LCD1.DB5, LCM1602_IIC1.D5
  N12: LCD1.DB6, LCM1602_IIC1.D6
  N13: LCD1.DB7, LCM1602_IIC1.D7
  N14: LCD1.LED+, LCM1602_IIC1.A
  N15: LCD1.LED-, LCM1602_IIC1.K
  N16: LCM1602_IIC1.SDA, Part1.A4/SDA
  N17: LCM1602_IIC1.SCL, Part1.A5/SCL
  N18: LCM1602_IIC1.LED_A, LCM1602_IIC1.LED_B
  N19: Q2.E, VCC1.-
  N20: Q2.B, Part1.D4
  N21: Q2.C, F1.GND
  N22: F1.5V, VCC1.+
  N23: KF-1.signal, Part1.D3_PWM
  N24: KF-1.C, Part3.+
  N25: KF-1.NO, LED2.C
  N26: Part3.-, LED2.A

custom parts:
  LCM1602 IIC: I2C-Module to use a 1602 or 2004 LCD on with the wire.h libory Serial LCD Modul
  Fan - Ventilador: Ventilador de 2 pines, se encuentra comunmente en computadoras de escritorio
  KF-301 Relay: KF-301
  LEDs: LEDs Standard schematic elements and footprints for 5mm, 3mm, 1206, and 0603 sized LEDs. 5mm - Spark Fun Electronics SKU : COM-00529 (and others)

// code stored in the sketch: Economical Food Dehydrator Using Refrigerator's Condenser's Waste Heat Assisted by Arduino Uno.ino
#include "DHT.h" 
#include <Wire.h> 
#define DHTPIN 2     // what pin we're connected to 
#define DHTTYPE DHT22   // DHT 22  (AM2302) 
#define fan 4 
#define relay 3 
#include <LiquidCrystal_I2C.h> 
LiquidCrystal_I2C lcd = LiquidCrystal_I2C(0x27, 16, 2); 
  
int maxTemp = 35; 
int minTemp = 30; 
int maxHum = 70; 
int minHum = 60; 
  
  
DHT dht(DHTPIN, DHTTYPE); 
  
void setup() { 
  pinMode(relay, OUTPUT); 
    pinMode(fan, OUTPUT); 
  Serial.begin(9600); 
    dht.begin(); 
    lcd.begin(16,2); 
    lcd.init(); 
  lcd.backlight(); 
} 
  
void loop() { 
  // Wait a few seconds between measurements. 
  delay(2000); 
  
  // Reading temperature or humidity takes about 250 milliseconds! 
  // Sensor readings may also be up to 2 seconds 'old' (its a very slow sensor) 
  float h = dht.readHumidity(); 
  // Read temperature as Celsius 
  float t = dht.readTemperature(); 
  
  // Check if any reads failed and exit early (to try again). 
  if (isnan(h) || isnan(t)) { 
    Serial.println("Failed to read from DHT sensor!"); 
    return; 
  } 
  
      if( t < minTemp) { // if temp is lower than minimum temp 
      // Heater on 
      digitalWrite(relay, 255); 
   } 
    if( t > maxTemp ) { // if temp is higher than maximum temp 
      // Heater off 
     analogWrite(relay, LOW); 
   } 
     if( h > maxHum) { // if hum is higher than maximum hum 
      // fan is spinning 
      analogWrite(fan, 255); 
   } 
    if( h < minHum ) { // if hum is lower than minimum hum 
      // fan is not spinning 
      digitalWrite(fan, LOW); 
   } 
  
  Serial.print("Humidity: "); 
  Serial.print(h); 
  Serial.print(" %\t"); 
  Serial.print("Temperature: "); 
  Serial.print(t); 
  Serial.println(" *C "); 
    
    lcd.clear(); 
    lcd.setCursor(0,0); 
    lcd.print("Temp: "); 
    lcd.print(t); 
    lcd.print(" "); 
    lcd.print((char)223); 
    lcd.print("C"); 
     lcd.setCursor(0,1); 
    lcd.print("Hum: "); 
     lcd.print(h); 
    lcd.print(" %"); 
    delay(1000); //Delay 1 sec. 
}

// code stored in the sketch: JEJE.ino
#include "DHT.h" 
#include <Wire.h> 
#define DHTPIN 2     // what pin we're connected to 
#define DHTTYPE DHT22   // DHT 22  (AM2302) 
#define fan 4 
#define relay 3 
#include <LiquidCrystal_I2C.h> 
LiquidCrystal_I2C lcd = LiquidCrystal_I2C(0x27, 16, 2); 
  
int maxTemp = 35; 
int minTemp = 30; 
int maxHum = 70; 
int minHum = 60; 
  
  
DHT dht(DHTPIN, DHTTYPE); 
  
void setup() { 
  pinMode(relay, OUTPUT); 
    pinMode(fan, OUTPUT); 
  Serial.begin(9600); 
    dht.begin(); 
    lcd.begin(16,2); 
    lcd.init(); 
  lcd.backlight(); 
} 
  
void loop() { 
  // Wait a few seconds between measurements. 
  delay(2000); 
  
  // Reading temperature or humidity takes about 250 milliseconds! 
  // Sensor readings may also be up to 2 seconds 'old' (its a very slow sensor) 
  float h = dht.readHumidity(); 
  // Read temperature as Celsius 
  float t = dht.readTemperature(); 
  
  // Check if any reads failed and exit early (to try again). 
  if (isnan(h) || isnan(t)) { 
    Serial.println("Failed to read from DHT sensor!"); 
    return; 
  } 
  
      if( t < minTemp) { // if temp is lower than minimum temp 
      ; // Heater on 
      digitalWrite(relay, 255); 
   } 
    if( t > maxTemp ) { // if temp is higher than maximum temp 
      // Heater off 
     analogWrite(relay, LOW); 
   } 
     if( h > maxHum) { // if hum is higher than maximum temp 
      ; // fan is not spinning 
      analogWrite(fan, 255); 
   } 
    if( h < minHum ) { // if hum is lower than minimum temp 
      // fan is not spinning 
      digitalWrite(fan, LOW); 
   } 
  
  Serial.print("Humidity: "); 
  Serial.print(h); 
  Serial.print(" %\t"); 
  Serial.print("Temperature: "); 
  Serial.print(t); 
  Serial.println(" *C "); 
    
    lcd.clear(); 
    lcd.setCursor(0,0); 
    lcd.print("Temp: "); 
    lcd.print(t); 
    lcd.print(" "); 
    lcd.print((char)223); 
    lcd.print("C"); 
     lcd.setCursor(0,1); 
    lcd.print("Hum: "); 
     lcd.print(h); 
    lcd.print(" %"); 
    delay(1000); //Delay 1 sec. 
}
